# Fritzing sketch ffritzingb1 (saved by Fritzing 0.9.5d)
breadboards: 1

parts:
  Mod1 = Heltec WiFi Kit 32 (V3) [part_number=HTIT-WB32_V3]
  R1 = Resistor [tolerance=±5% resistance=220 package=THT]
  LED1 = LED - 5mm [color="Red (660nm)" package="5 mm [THT]"]
  S1 = Pushbutton [package="[THT]"]

nets:
  N1: Mod1.pin_18, Mod1.pin_19, Mod1.pin_35
  N2: R1.Pin_1, LED1.anode
  N3: S1.Pin_1, S1.Pin_2
  N4: S1.Pin_3, S1.Pin_4

custom parts:
  Heltec WiFi Kit 32 (V3): The Heltec WiFi Kit 32 is an IoT development board designed and produced by Heltec Automation and based on the Espressif ESP32. The board includes WiFi, Bluetooth, as well as a 0.96″ 128*64 dot matrix OLED display and a lithium battery management system.
